# Fritzing sketch Schaltbild Lightpaintingstab (saved by Fritzing 0.9.0b)
stripboards: 1

parts:
  Bauteil1 = Arduino Uno (Rev3)
  LED1 = Super Flux LED blue [color=Blue]
  LED2 = Super Flux LED blue [color=Blue]
  LED3 = Super Flux LED blue [color=Blue]
  LED4 = Super Flux LED blue [color=Blue]
  LED5 = Super Flux LED blue [color=Blue]
  LED6 = Super Flux LED blue [color=Blue]
  LED7 = Super Flux LED blue [color=Blue]
  LED8 = Super Flux LED blue [color=Blue]
  LED9 = Super Flux LED blue [color=Blue]
  LED10 = Super Flux LED blue [color=Blue]
  LED11 = Super Flux LED blue [color=Blue]
  LED12 = Super Flux LED blue [color=Blue]
  LED13 = Super Flux LED blue [color=Blue]
  LED19 = Super Flux LED blue [color=Blue]
  LED22 = Super Flux LED blue [color=Blue]
  LED23 = Super Flux LED blue [color=Blue]
  VCC1 = Battery block 9V
  C1 = Tantalum Capacitor [capacitance=1μF package="100 mil [THT, tantalum]"]
  S1 = Pushbutton [package="[THT]"]
  Q1 = Basic FET P-Channel [package="TO220 [THT]"]
  C2 = Tantalum Capacitor [capacitance=1μF package="100 mil [THT, tantalum]"]
  R1 = Resistor [tolerance=±5% resistance=470 package=THT]

nets:
  N1: Bauteil1.GND, S1.Pin_3, S1.Pin_4
  N2: Bauteil1.D0/RX, R1.Pin_0
  N3: Bauteil1.D2, S1.Pin_1, S1.Pin_2
  N4: LED1.anode, LED6.cathode
  N5: LED1.cathode, LED22.anode
  N6: LED2.anode, LED11.cathode
  N7: LED2.cathode, LED3.anode
  N8: LED3.cathode, LED4.anode
  N9: LED4.cathode, LED5.anode
  N10: LED5.cathode, LED6.anode
  N11: LED7.anode, LED12.cathode
  N12: LED7.cathode, LED9.anode
  N13: LED8.anode, LED19.cathode
  N14: LED8.cathode, LED12.anode
  N15: LED9.cathode, LED10.anode
  N16: LED10.cathode, LED11.anode
  N17: LED13.anode, LED23.cathode
  N18: LED13.cathode, LED19.anode
  N19: LED23.anode, VCC1.-, VCC1.+, C1.-, C1.+, Q1.gate, Q1.drain, Q1.source, C2.-, C2.+
